# Fritzing sketch circuit (saved by Fritzing 0.8.5b)
breadboards: 1

parts:
  Part1 = Arduino Leonardo (Rev3b)
  R1 = Photocell (LDR) [package=THT]
  R2 = Photocell (LDR) [package=THT]
  R3 = Resistor [tolerance=±5% resistance=220 package=THT]
  LED1 = LED - 5mm [color="Red (633nm)" package="5 mm [THT]"]

nets:
  N1: Part1.5V, R1.pin_0
  N2: Part1.GND, R2.pin_1, R3.Pin_0
  N3: Part1.A0, R1.pin_1, R2.pin_0
  N4: Part1.D11_PWM, LED1.anode
  N5: R3.Pin_1, LED1.cathode
